// Logisim project 4_bit_ALU.circ as structural Verilog: 3 circuits, main circuit ALU-1bit
module ALU_1bit (
  input  C_in,
  input  S1_prime,
  input  A,
  input  B,
  input  S0_prime,
  output SUM,
  output C_out
);

  wire and_1_out, or_1_out;

  or or_1 (or_1_out, B, S0_prime);
  and and_1 (and_1_out, C_in, S1_prime);
  Adder #(.width(1)) adder_1 (.a(A), .b(or_1_out), .out(SUM), .cin(and_1_out), .cout(C_out));
endmodule

module ALU_4bit (
  input  [3:0] A,
  input  [3:0] B,
  input  [2:0] Selector,
  output [3:0] Output,
  output [3:0] Flags
);

  wire alu_1bit_1_c_out, alu_1bit_2_c_out, alu_1bit_3_c_out, alu_1bit_4_c_out, clock_1_out, not_1_out,
       not_2_out, not_3_out, OF_out, or_1_out, or_2_out, or_3_out, or_4_out;

  not not_1 (not_1_out, Selector[0]);
  not not_2 (not_2_out, Selector[1]);
  or or_1 (or_1_out, Selector[0], not_2_out);
  ALU_1bit alu_1bit_1 (
    .C_in(Selector[2]), .S1_prime(not_2_out), .A(A[0]), .B(B[0]), .S0_prime(not_1_out), .SUM(Output[0]),
    .C_out(alu_1bit_1_c_out));
  ALU_1bit alu_1bit_2 (
    .C_in(alu_1bit_1_c_out), .S1_prime(not_2_out), .A(A[1]), .B(B[1]), .S0_prime(not_1_out), .SUM(Output[1]),
    .C_out(alu_1bit_2_c_out));
  ALU_1bit alu_1bit_3 (
    .C_in(alu_1bit_2_c_out), .S1_prime(not_2_out), .A(A[2]), .B(B[2]), .S0_prime(not_1_out), .SUM(Output[2]),
    .C_out(alu_1bit_3_c_out));
  ALU_1bit alu_1bit_4 (
    .C_in(alu_1bit_3_c_out), .S1_prime(not_2_out), .A(A[3]), .B(B[3]), .S0_prime(not_1_out), .SUM(Output[3]),
    .C_out(alu_1bit_4_c_out));
  or or_2 (or_2_out, Output[3], Output[2]);
  or or_3 (or_3_out, or_2_out, or_4_out);
  or or_4 (or_4_out, Output[1], Output[0]);
  xor OF (OF_out, alu_1bit_4_c_out, alu_1bit_3_c_out);
  not not_3 (not_3_out, or_3_out);
  Register #(.width(1)) ZF (.D(not_3_out), .en(or_1_out), .Q(Flags[0]), .clk(clock_1_out));  // open: clr
  Register #(.width(1)) OF_2 (.D(OF_out), .en(not_2_out), .Q(Flags[1]), .clk(clock_1_out), .clr(Selector[1]));
  Register #(.width(1)) SF (.D(Output[3]), .en(or_1_out), .Q(Flags[2]), .clk(clock_1_out));  // open: clr
  Register #(.width(1)) CF (.D(alu_1bit_4_c_out), .en(not_2_out), .Q(Flags[3]), .clk(clock_1_out), .clr(Selector[1]));
  Clock clock_1 (.out(clock_1_out));

  // Notes on the sheet:
  //   CS2_CS1_CS0
  //   CF, SF, OF, ZF
endmodule

module ALU_4bit_Simulation (
  input  [3:0] A,
  input  [3:0] B,
  input  [2:0] CS2_CS1_CS0,
  output [3:0] Flags,
  output [3:0] Result
);

  ALU_4bit alu_4bit_1 (.A(A), .B(B), .Selector(CS2_CS1_CS0), .Output(Result), .Flags(Flags));

  // Notes on the sheet:
  //   CF, SF, OF, ZF
endmodule
