// Logisim project FPA.circ as structural Verilog: 15 circuits, main circuit 1bit ALU
module _1bit_ALU (
  input  S0_prime,
  input  S1_prime,
  input  S2_prime,
  input  Cin,
  input  S2,
  input  S1,
  input  S0,
  input  A,
  input  B,
  output Sum,
  output Cout
);

  wire and_1_out, and_2_out, and_3_out, and_4_out, and_5_out, not_1_out, or_1_out, or_2_out;

  not not_1 (not_1_out, B);
  and and_1 (and_1_out, S2, S1_prime, S0_prime, B);
  and and_2 (and_2_out, S2, S1, S0_prime, not_1_out);
  and and_3 (and_3_out, S0, B);
  and and_4 (and_4_out, S1, not_1_out);
  or or_1 (or_1_out, and_1_out, and_2_out, A);
  or or_2 (or_2_out, and_3_out, and_4_out);
  and and_5 (and_5_out, Cin, S2_prime);
  Adder #(.width(1)) adder_1 (.a(or_1_out), .b(or_2_out), .out(Sum), .cin(and_5_out), .cout(Cout));
endmodule

module _4bit_ALU (
  input  [2:0] S2_S1_S0,
  input  Cin,
  input  [3:0] A,
  input  [3:0] B,
  output [3:0] Result,
  output Cout
);

  wire n1bit_alu_1_cout, n1bit_alu_2_cout, n1bit_alu_3_cout, not_1_out, not_2_out, not_3_out;

  not not_1 (not_1_out, S2_S1_S0[0]);
  not not_2 (not_2_out, S2_S1_S0[1]);
  not not_3 (not_3_out, S2_S1_S0[2]);
  _1bit_ALU u_1bit_alu_1 (
    .Cin(Cin), .S2(S2_S1_S0[2]), .S1(S2_S1_S0[1]), .S0(S2_S1_S0[0]), .A(A[0]), .B(B[0]), .Sum(Result[0]),
    .Cout(n1bit_alu_1_cout), .S0_prime(not_1_out), .S1_prime(not_2_out), .S2_prime(not_3_out));
  _1bit_ALU u_1bit_alu_2 (
    .Cin(n1bit_alu_1_cout), .S2(S2_S1_S0[2]), .S1(S2_S1_S0[1]), .S0(S2_S1_S0[0]), .A(A[1]), .B(B[1]),
    .Sum(Result[1]), .Cout(n1bit_alu_2_cout), .S0_prime(not_1_out), .S1_prime(not_2_out), .S2_prime(not_3_out));
  _1bit_ALU u_1bit_alu_3 (
    .Cin(n1bit_alu_2_cout), .S2(S2_S1_S0[2]), .S1(S2_S1_S0[1]), .S0(S2_S1_S0[0]), .A(A[2]), .B(B[2]),
    .Sum(Result[2]), .Cout(n1bit_alu_3_cout), .S0_prime(not_1_out), .S1_prime(not_2_out), .S2_prime(not_3_out));
  _1bit_ALU u_1bit_alu_4 (
    .Cin(n1bit_alu_3_cout), .S2(S2_S1_S0[2]), .S1(S2_S1_S0[1]), .S0(S2_S1_S0[0]), .A(A[3]), .B(B[3]),
    .Sum(Result[3]), .Cout(Cout), .S0_prime(not_1_out), .S1_prime(not_2_out), .S2_prime(not_3_out));
endmodule

module _8bit_ALU (
  input  Cin,
  input  [2:0] S2_S1_S0,
  input  [7:0] A_8bit,
  input  [7:0] B_8bit,
  output [7:0] Result,
  output Cout
);

  wire n4bit_alu_1_cout;

  _4bit_ALU u_4bit_alu_1 (
    .S2_S1_S0(S2_S1_S0), .Cin(Cin), .A(A_8bit[3:0]), .B(B_8bit[3:0]), .Cout(n4bit_alu_1_cout),
    .Result(Result[3:0]));
  _4bit_ALU u_4bit_alu_2 (
    .S2_S1_S0(S2_S1_S0), .Cin(n4bit_alu_1_cout), .A(A_8bit[7:4]), .B(B_8bit[7:4]), .Cout(Cout),
    .Result(Result[7:4]));
endmodule

module _16bit_ALU (
  input  Cin,
  input  [2:0] S2_S1_S0,
  input  [15:0] A_16bit,
  input  [15:0] B_16bit,
  output [15:0] Result,
  output Cout
);

  wire n8bit_alu_1_cout;

  _8bit_ALU u_8bit_alu_1 (
    .Cin(Cin), .S2_S1_S0(S2_S1_S0), .A_8bit(A_16bit[7:0]), .B_8bit(B_16bit[7:0]), .Cout(n8bit_alu_1_cout),
    .Result(Result[7:0]));
  _8bit_ALU u_8bit_alu_2 (
    .Cin(n8bit_alu_1_cout), .S2_S1_S0(S2_S1_S0), .A_8bit(A_16bit[15:8]), .B_8bit(B_16bit[15:8]), .Cout(Cout),
    .Result(Result[15:8]));
endmodule

module _16bit_Separator (
  input  [15:0] Number,
  output Has_zero,
  output [13:0] Sign_01_Fraction,
  output [3:0] Exponent
);

  wire [3:0] bitfinder_1_index;
  wire [14:0] bit_extender_1_out;

  Bit_Extender #(.in_width(16), .out_width(15)) bit_extender_1 (.in(Number), .out(bit_extender_1_out));
  BitFinder #(.width(15), .\type ("high1")) bitfinder_1 (
    .in(bit_extender_1_out), .index(bitfinder_1_index));  // open: found
  Comparator #(.width(4)) comparator_1 (.a(bitfinder_1_index), .b(4'b0000), .eq(Has_zero));  // open: gt, lt
  not not_1 (Sign_01_Fraction[11], Has_zero);

  assign Exponent = Number[14:11];
  assign {Sign_01_Fraction[13:12], Sign_01_Fraction[10:0]} = {Number[15], 1'b0, Number[10:0]};
endmodule

module _16bit_OperandSelector (
  input  [15:0] Num_B,
  input  [15:0] Num_A,
  output Contains_zero,
  output [3:0] Exponent,
  output [13:0] Bigger_Number,
  output [13:0] Smaller_Number
);

  wire n4bit_alu_1_cout, n16bit_separator_1_has_zero, n16bit_separator_2_has_zero;
  wire [3:0] multiplexer_3_out, n4bit_alu_1_result, n16bit_separator_1_exponent, n16bit_separator_2_exponent,
       negator_1_out;
  wire [13:0] multiplexer_2_out, n16bit_separator_1_sign_01_fraction, n16bit_separator_2_sign_01_fraction;

  _16bit_Separator u_16bit_separator_1 (
    .Number(Num_B), .Sign_01_Fraction(n16bit_separator_1_sign_01_fraction),
    .Exponent(n16bit_separator_1_exponent), .Has_zero(n16bit_separator_1_has_zero));
  _4bit_ALU u_4bit_alu_1 (
    .S2_S1_S0(3'b010), .Cin(1'b1), .A(n16bit_separator_2_exponent), .B(n16bit_separator_1_exponent),
    .Cout(n4bit_alu_1_cout), .Result(n4bit_alu_1_result));
  Negator #(.width(4)) negator_1 (.in(n4bit_alu_1_result), .out(negator_1_out));
  Multiplexer #(.width(14)) multiplexer_1 (
    .in0(n16bit_separator_1_sign_01_fraction), .in1(n16bit_separator_2_sign_01_fraction),
    .out(Bigger_Number), .sel(n4bit_alu_1_cout));  // open: en
  Multiplexer #(.width(14)) multiplexer_2 (
    .in0(n16bit_separator_2_sign_01_fraction), .in1(n16bit_separator_1_sign_01_fraction),
    .out(multiplexer_2_out), .sel(n4bit_alu_1_cout));  // open: en
  Multiplexer #(.width(4)) multiplexer_3 (
    .in0(negator_1_out), .in1(n4bit_alu_1_result), .out(multiplexer_3_out), .sel(n4bit_alu_1_cout));  // open: en
  _16bit_Separator u_16bit_separator_2 (
    .Number(Num_A), .Sign_01_Fraction(n16bit_separator_2_sign_01_fraction),
    .Exponent(n16bit_separator_2_exponent), .Has_zero(n16bit_separator_2_has_zero));
  Multiplexer #(.width(4)) multiplexer_4 (
    .in0(n16bit_separator_1_exponent), .in1(n16bit_separator_2_exponent), .out(Exponent),
    .sel(n4bit_alu_1_cout));  // open: en
  or or_1 (Contains_zero, n16bit_separator_1_has_zero, n16bit_separator_2_has_zero);
  _14bit_RightShifter u_14bit_rightshifter_1 (
    .Input_Number(multiplexer_2_out), .Number_of_Shift(multiplexer_3_out),
    .Number_after_Shifting(Smaller_Number));

  // Notes on the sheet:
  //   Reference
  //   Digital Logic and Computer Design by M. Morris Mano  ---> Page 330
  //   Difference
  //   Smaller Number
  //   Exponent Difference
  //   Resultant Exponent
  //   Bigger Number
endmodule

module _14bit_RightShifter (
  input  [13:0] Input_Number,
  input  [3:0] Number_of_Shift,
  output [13:0] Number_after_Shifting
);

  Shifter #(.width(13), .shift("lr")) shifter_1 (
    .in(Input_Number[12:0]), .\dist (Number_of_Shift), .out(Number_after_Shifting[12:0]));

  assign Number_after_Shifting[13] = Input_Number[13];

  // Notes on the sheet:
  //   Sign bit won't shift
endmodule

module _16bit_AddendCreator (
  input  [13:0] Number_A,
  output [15:0] Addend
);

  wire [15:0] bit_extender_1_out, negator_1_out;

  assign bit_extender_1_out = {{3{1'b0}}, Number_A[12:0]};  // Bit_Extender bit_extender_1
  Negator #(.width(16)) negator_1 (.in(bit_extender_1_out), .out(negator_1_out));
  Multiplexer #(.width(16)) multiplexer_1 (
    .in0(bit_extender_1_out), .in1(negator_1_out), .out(Addend), .sel(Number_A[13]));  // open: en
endmodule

module _16bit_14bit_ResultFormater (
  input  [15:0] Number,
  output [13:0] Result,
  output Sign
);

  wire [15:0] negator_1_out;
  wire [15:14] multiplexer_1_out;

  Negator #(.width(16)) negator_1 (.in(Number), .out(negator_1_out));
  Multiplexer #(.width(16)) multiplexer_1 (
    .in0(Number), .in1(negator_1_out), .out({multiplexer_1_out, Result}), .sel(Number[13]));  // open: en

  assign Sign = Number[13];
endmodule

module SignificantAdder (
  input  [13:0] Number_A,
  input  [13:0] Number_B,
  output [13:0] Result,
  output Sign
);

  wire [15:0] n16bit_addendcreator_1_addend, n16bit_addendcreator_2_addend, n16bit_alu_1_result;

  _16bit_AddendCreator u_16bit_addendcreator_1 (.Number_A(Number_A), .Addend(n16bit_addendcreator_1_addend));
  _16bit_AddendCreator u_16bit_addendcreator_2 (.Number_A(Number_B), .Addend(n16bit_addendcreator_2_addend));
  _16bit_ALU u_16bit_alu_1 (
    .Cin(1'b0), .S2_S1_S0(3'b001), .A_16bit(n16bit_addendcreator_1_addend),
    .B_16bit(n16bit_addendcreator_2_addend), .Result(n16bit_alu_1_result));  // open: Cout
  _16bit_14bit_ResultFormater Result_Formater (.Number(n16bit_alu_1_result), .Result(Result), .Sign(Sign));
endmodule

module NormalizerLeftShift (
  input  [13:0] _14bit_Input,
  input  [3:0] exponent,
  output [13:0] _14bit_output,
  output [3:0] Exponent_2,
  output Underflow
);

  wire [3:0] bitfinder_1_index, subtractor_1_out;
  wire [11:0] bit_extender_1_out;

  Bit_Extender #(.in_width(14), .out_width(12)) bit_extender_1 (.in(_14bit_Input), .out(bit_extender_1_out));
  BitFinder #(.width(12), .\type ("high1")) bitfinder_1 (
    .in(bit_extender_1_out), .index(bitfinder_1_index));  // open: found
  Subtractor #(.width(4)) subtractor_1 (
    .a(4'b1011), .b(bitfinder_1_index), .out(subtractor_1_out), .bin(1'b0));  // open: bout
  Shifter #(.width(14)) shifter_1 (.in(_14bit_Input), .\dist (subtractor_1_out), .out(_14bit_output));
  Subtractor #(.width(4)) subtractor_2 (
    .a(exponent), .b(subtractor_1_out), .out(Exponent_2), .bin(1'b0), .bout(Underflow));

  // Notes on the sheet:
  //   fraction 11 bit. b=11
  //   finds index of highest order 1
  //   indexing start from right to left
  //   count start from 0
endmodule

module NormalizerRightShift (
  input  [13:0] Input,
  input  [3:0] Exp_in,
  output [13:0] Ouput,
  output [3:0] Exp_out,
  output Overflow
);

  wire adder_1_cout, comparator_1_eq;

  Shifter #(.width(14), .shift("lr")) shifter_1 (.in(Input), .\dist (4'b0001), .out(Ouput));
  Adder #(.width(4)) adder_1 (.a(Exp_in), .b(4'b0001), .out(Exp_out), .cin(1'b0), .cout(adder_1_cout));
  Comparator #(.width(4), .mode("unsigned")) comparator_1 (
    .a(Exp_out), .b(4'b1111), .eq(comparator_1_eq));  // open: gt, lt
  or or_1 (Overflow, comparator_1_eq, adder_1_cout);
endmodule

module Normalizer (
  input  [3:0] Exp_in,
  input  [13:0] Significant_in,
  input  Sign,
  input  Has_0,
  output [15:0] Output,
  output Overflow,
  output Underflow
);

  wire and_1_out, and_2_out, and_3_out, and_4_out, and_5_out, and_6_out, comparator_1_eq,
       normalizerleftshift_1_underflow, normalizerrightshift_1_overflow, not_1_out, not_2_out, not_3_out,
       or_1_out;
  wire [3:0] bitfinder_1_index, multiplexer_2_out, multiplexer_3_out, normalizerleftshift_1_exponent_2,
       normalizerrightshift_1_exp_out;
  wire [12:0] bit_extender_1_out;
  wire [13:0] multiplexer_1_out, normalizerleftshift_1__14bit_output, normalizerrightshift_1_ouput;
  wire [13:11] multiplexer_4_out;

  Bit_Extender #(.in_width(14), .out_width(13)) bit_extender_1 (.in(Significant_in), .out(bit_extender_1_out));
  BitFinder #(.width(13), .\type ("high1")) bitfinder_1 (
    .in(bit_extender_1_out), .index(bitfinder_1_index));  // open: found
  Comparator #(.width(4)) comparator_1 (.a(bitfinder_1_index), .b(4'b0000), .eq(comparator_1_eq));  // open: gt, lt
  NormalizerLeftShift normalizerleftshift_1 (
    ._14bit_Input(Significant_in), .exponent(Exp_in), ._14bit_output(normalizerleftshift_1__14bit_output),
    .Exponent_2(normalizerleftshift_1_exponent_2), .Underflow(normalizerleftshift_1_underflow));
  NormalizerRightShift normalizerrightshift_1 (
    .Input(Significant_in), .Exp_in(Exp_in), .Ouput(normalizerrightshift_1_ouput),
    .Exp_out(normalizerrightshift_1_exp_out), .Overflow(normalizerrightshift_1_overflow));
  or or_1 (or_1_out, comparator_1_eq, Has_0);
  Multiplexer #(.width(14)) multiplexer_1 (
    .in0(normalizerleftshift_1__14bit_output), .in1(normalizerrightshift_1_ouput), .out(multiplexer_1_out),
    .sel(Significant_in[12]));  // open: en
  Multiplexer #(.width(4)) multiplexer_2 (
    .in0(normalizerleftshift_1_exponent_2), .in1(normalizerrightshift_1_exp_out), .out(multiplexer_2_out),
    .sel(Significant_in[12]));  // open: en
  Multiplexer #(.width(4)) multiplexer_3 (
    .in0(multiplexer_2_out), .in1(Exp_in), .out(multiplexer_3_out), .sel(or_1_out));  // open: en
  Multiplexer #(.width(14)) multiplexer_4 (
    .in0(multiplexer_1_out), .in1(Significant_in), .out({multiplexer_4_out, Output[10:0]}), .sel(or_1_out));  // open: en
  Multiplexer #(.width(4)) multiplexer_5 (
    .in0(multiplexer_3_out), .in1(4'b0000), .out(Output[14:11]), .sel(comparator_1_eq));  // open: en
  not not_1 (not_1_out, normalizerleftshift_1_underflow);
  and and_1 (and_1_out, Output[11], Output[12]);
  and and_2 (and_2_out, Output[13], Output[14]);
  and and_3 (and_3_out, normalizerrightshift_1_overflow, Significant_in[12]);
  not not_2 (not_2_out, Significant_in[12]);
  and and_4 (and_4_out, not_2_out, normalizerleftshift_1_underflow);
  and and_5 (and_5_out, and_1_out, and_2_out);
  and and_6 (and_6_out, and_5_out, not_1_out);
  or or_2 (Overflow, and_3_out, and_6_out);
  and and_7 (Underflow, and_4_out, not_3_out);
  not not_3 (not_3_out, or_1_out);

  assign Output[15] = Sign;
endmodule

module _16bit_FloatingPointAdder (
  input  [15:0] Number_A,
  input  [15:0] Number_B,
  output [15:0] Output,
  output Overflow,
  output Underflow
);

  wire n16bit_operandselector_1_contains_zero, significantadder_1_sign;
  wire [3:0] n16bit_operandselector_1_exponent;
  wire [13:0] n16bit_operandselector_1_bigger_number, n16bit_operandselector_1_smaller_number,
       significantadder_1_result;

  SignificantAdder significantadder_1 (
    .Number_A(n16bit_operandselector_1_bigger_number), .Number_B(n16bit_operandselector_1_smaller_number),
    .Result(significantadder_1_result), .Sign(significantadder_1_sign));
  _16bit_OperandSelector u_16bit_operandselector_1 (
    .Exponent(n16bit_operandselector_1_exponent), .Bigger_Number(n16bit_operandselector_1_bigger_number),
    .Smaller_Number(n16bit_operandselector_1_smaller_number), .Num_B(Number_B), .Num_A(Number_A),
    .Contains_zero(n16bit_operandselector_1_contains_zero));
  Normalizer normalizer_1 (
    .Exp_in(n16bit_operandselector_1_exponent), .Significant_in(significantadder_1_result),
    .Sign(significantadder_1_sign), .Output(Output), .Overflow(Overflow), .Underflow(Underflow),
    .Has_0(n16bit_operandselector_1_contains_zero));
endmodule

module SimulatorCircuit (
  input  [15:0] Number_A,
  input  [15:0] Number_B,
  output [15:0] Output,
  output Overflow,
  output Underflow
);

  _16bit_FloatingPointAdder u_16bit_floatingpointadder_1 (
    .Output(Output), .Overflow(Overflow), .Underflow(Underflow), .Number_A(Number_A), .Number_B(Number_B));
endmodule
