// Logisim project Processor.circ as structural Verilog: 6 circuits, main circuit main
module main (
  output [7:0] Register_Values,
  output [7:0] out_2,
  output [7:0] out_3,
  output [7:0] out_4,
  output [7:0] out_5,
  output [7:0] out_6,
  output [7:0] out_7
);

  wire alu_src, and_1_out, and_2_out, beq, bneq, br_jump, Clock, jump, L_R_prime, mem_read, mem_to_reg,
       mem_write, \nor , not_2_out, reg_dst, reg_write, reset, shift, zero_t;
  wire [3:0] alu_op, multiplexer_1_out, opcode, RD, RS, RT, SHAMT;
  wire [7:0] addr_imm, alu_out, dmem_in, dmem_out, instruction_counter_1_pc, Mem2RegW, multiplexer_2_out,
       multiplexer_4_out, not_1_out, R1, R2, Sout;
  wire [19:0] rom_1_data;

  Button CLK (.out(Clock));
  Button u_Reset (.out(reset));
  ROM #(.dataWidth(20)) rom_1 (.addr(instruction_counter_1_pc), .data(rom_1_data));  // open: sel
  Instruction_Counter instruction_counter_1 (
    .Shift_Amt(addr_imm), .out_7(opcode), .out_8(RS), .out_9(RT), .out_10(RD), .out_11(SHAMT),
    .out_12(addr_imm), .RESET(reset), .CLK(Clock), .in_2(br_jump), .in_6(rom_1_data),
    .PC(instruction_counter_1_pc), .in_3(jump));
  Multiplexer #(.width(4)) multiplexer_1 (.in0(RT), .in1(RD), .out(multiplexer_1_out), .sel(reg_dst));  // open: en
  Registers registers_1 (
    .in_1(RS), .in_2(Clock), .in_3(reg_write), .in_4(RT), .in_6(multiplexer_1_out), .out_10(R1), .out_12(R2),
    .in_7(Mem2RegW), .in_5(reset), .out_8(Register_Values), .out_9(out_2), .out_11(out_3), .out_13(out_4),
    .out_14(out_5), .out_15(out_6), .out_16(out_7));
  RAM #(.bus("separate")) ram_1 (
    .addr(dmem_in), .din(R2), .data(dmem_out), .str(mem_write), .sel(1'b1), .clk(Clock), .ld(mem_read));  // open: clr
  Multiplexer #(.width(8)) multiplexer_2 (
    .in0(R2), .in1(addr_imm), .out(multiplexer_2_out), .sel(alu_src));  // open: en
  assign not_1_out = ~alu_out;  // NOT_Gate not_1, 8 bits wide
  _8bit_ALU u_8bit_alu_1 (
    .A_8bit(R1), .B_8bit(multiplexer_2_out), .Result(alu_out), .CLR(reset), .EN(1'b1), .out_8(zero_t),
    .CLK(Clock), .in_1(alu_op));  // open: Cout
  Shifter shifter_1 (.Value(R2), .SHAMT(SHAMT), .in_3(L_R_prime), .Output(Sout));
  Multiplexer #(.width(8)) multiplexer_3 (.in0(alu_out), .in1(not_1_out), .out(dmem_in), .sel(\nor ));  // open: en
  not not_2 (not_2_out, zero_t);
  Multiplexer #(.width(8)) multiplexer_4 (
    .in0(dmem_in), .in1(dmem_out), .out(multiplexer_4_out), .sel(mem_to_reg));  // open: en
  and and_1 (and_1_out, zero_t, beq);
  or or_1 (br_jump, and_1_out, and_2_out);
  and and_2 (and_2_out, not_2_out, bneq);
  Multiplexer #(.width(8)) multiplexer_5 (
    .in0(multiplexer_4_out), .in1(Sout), .out(Mem2RegW), .sel(shift));  // open: en
  CONTROL control_1 (
    .OpCode(opcode), .Shift(shift), .JUMP(jump), .Left_Right_prime(L_R_prime), .BNEQ(bneq), .NOR(\nor ),
    .RegWrite(reg_write), .ALUSrc(alu_src), .MemWrite(mem_write), .ALUOp(alu_op), .MemtoReg(mem_to_reg),
    .MemRead(mem_read), .BEQ(beq), .RegDest(reg_dst));

  // Other names for the same wires on the sheet: sp[7:0] = out_7; t0[7:0] = Register_Values; t1[7:0] = out_2;
  //   t2[7:0] = out_3; t3[7:0] = out_4; t4[7:0] = out_5; zero[7:0] = out_6

  // Notes on the sheet:
  //   contents of rom_1 (hex, n*v repeats v):
  //   80100 3500f 80900 25030 80b00 4520a 80700 22540 80300 351f4 80500
  //   1
  //   2
  //   5
  //   DATA-Memory
  //   3
  //   SHIFT
  //   4
  //   0
  //   Branch
endmodule

module Registers (
  input  [3:0] in_1,
  input  in_2,
  input  in_3,
  input  [3:0] in_4,
  input  in_5,
  input  [3:0] in_6,
  input  [7:0] in_7,
  output [7:0] out_8,
  output [7:0] out_9,
  output [7:0] out_10,
  output [7:0] out_11,
  output [7:0] out_12,
  output [7:0] out_13,
  output [7:0] out_14,
  output [7:0] out_15,
  output [7:0] out_16
);

  wire demultiplexer_1_out0, demultiplexer_1_out1, demultiplexer_1_out2, demultiplexer_1_out3,
       demultiplexer_1_out4, demultiplexer_1_out5, demultiplexer_1_out6, or_1_out, stack_en, stack_selector;
  wire [7:0] register_8_q, stack_d;

  Multiplexer multiplexer_1 (.in0(stack_selector), .in1(1'b1), .out(stack_en), .sel(in_5));  // open: en
  Multiplexer #(.width(8)) multiplexer_2 (.in0(in_7), .in1({8{1'b1}}), .out(stack_d), .sel(in_5));  // open: en
  Demultiplexer #(.select(4)) demultiplexer_1 (
    .out0(demultiplexer_1_out0), .out1(demultiplexer_1_out1), .out2(demultiplexer_1_out2),
    .out3(demultiplexer_1_out3), .out4(demultiplexer_1_out4), .out5(demultiplexer_1_out5),
    .out6(demultiplexer_1_out6), .out7(stack_selector), .in(in_3), .sel(in_6), .en(1'b1));  // open: out8, out9, out10, out11, out12, out13, out14, out15
  Register #(.trigger("falling")) register_1 (.D(in_7), .en(demultiplexer_1_out0), .Q(out_8), .clk(in_2), .clr(in_5));
  Register #(.trigger("falling")) register_2 (.D(in_7), .en(demultiplexer_1_out3), .Q(out_13), .clk(in_2), .clr(in_5));
  Register #(.trigger("falling")) register_3 (.D(in_7), .en(demultiplexer_1_out1), .Q(out_9), .clk(in_2), .clr(in_5));
  Register #(.trigger("falling")) register_4 (.D(in_7), .en(demultiplexer_1_out4), .Q(out_14), .clk(in_2), .clr(in_5));
  Register #(.trigger("falling")) register_5 (.D(in_7), .en(demultiplexer_1_out2), .Q(out_11), .clk(in_2), .clr(in_5));
  Register #(.trigger("falling")) register_6 (
    .D({8{1'b0}}), .en(demultiplexer_1_out5), .Q(out_15), .clk(in_2), .clr(in_5));
  or or_1 (or_1_out, in_5, in_2);
  Register #(.trigger("falling")) register_7 (.D(stack_d), .en(stack_en), .Q(out_16), .clk(or_1_out));  // open: clr
  Register #(.trigger("falling")) register_8 (
    .D(in_7), .en(demultiplexer_1_out6), .Q(register_8_q), .clk(in_2), .clr(in_5));
  Multiplexer #(.select(4), .width(8)) multiplexer_3 (
    .in0(out_8), .in1(out_9), .in2(out_11), .in3(out_13), .in4(out_14), .in5(out_15), .in6(register_8_q),
    .in7(out_16), .out(out_10), .sel(in_1));  // open: in8, in9, in10, in11, in12, in13, in14, in15, en
  Multiplexer #(.select(4), .width(8)) multiplexer_4 (
    .in0(out_8), .in1(out_9), .in2(out_11), .in3(out_13), .in4(out_14), .in5(out_15), .in6(register_8_q),
    .in7(out_16), .out(out_12), .sel(in_4));  // open: in8, in9, in10, in11, in12, in13, in14, in15, en

  // Other names for the same wires on the sheet: clk = in_2; reg1_i[3:0] = in_1; reg1_o[7:0] = out_10;
  //   reg2_i[3:0] = in_4; reg2_o[7:0] = out_12; Reset = in_5; sp[7:0] = out_16; t0[7:0] = out_8; t1[7:0] = out_9;
  //   t2[7:0] = out_11; t3[7:0] = out_13; t4[7:0] = out_14; WE = in_3; write_data[7:0] = in_7; write_reg[3:0] = in_6;
  //   zero[7:0] = out_15
endmodule

module CONTROL (
  input  [3:0] OpCode,
  output Shift,
  output JUMP,
  output Left_Right_prime,
  output BNEQ,
  output NOR,
  output RegWrite,
  output ALUSrc,
  output MemWrite,
  output [3:0] ALUOp,
  output MemtoReg,
  output MemRead,
  output BEQ,
  output RegDest
);

  ROM #(.addrWidth(4), .dataWidth(16)) rom_1 (
    .addr(OpCode),
    .data({RegDest, BEQ, MemRead, MemtoReg, ALUOp, MemWrite, ALUSrc, RegWrite, NOR, BNEQ, Left_Right_prime, JUMP, Shift}));  // open: sel

  // Notes on the sheet:
  //   contents of rom_1 (hex, n*v repeats v):
  //   860 c60 8220 260 560 4500 8830 3260 2 508 12e0 8025 8c20 8520 8021 8820
endmodule

module Instruction_separator (
  input  [19:0] Instruction,
  output [7:0] Imm_Addr,
  output [3:0] SHIFT_AMNT,
  output [3:0] DST_REG,
  output [3:0] SRC_REG2,
  output [3:0] SRC_REG1,
  output [3:0] OP_CODE
);


  assign DST_REG = Instruction[7:4];
  assign Imm_Addr = Instruction[7:0];
  assign OP_CODE = Instruction[19:16];
  assign SHIFT_AMNT = Instruction[3:0];
  assign SRC_REG1 = Instruction[15:12];
  assign SRC_REG2 = Instruction[11:8];
endmodule

module Instruction_Counter (
  input  [7:0] Shift_Amt,
  input  in_2,
  input  in_3,
  input  RESET,
  input  CLK,
  input  [19:0] in_6,
  output [3:0] out_7,
  output [3:0] out_8,
  output [3:0] out_9,
  output [3:0] out_10,
  output [3:0] out_11,
  output [7:0] out_12,
  output [7:0] PC
);

  wire [7:0] adder_1_out, adder_2_out, multiplexer_1_out, multiplexer_2_out;

  Register #(.trigger("falling")) u_PC (.D(multiplexer_2_out), .en(1'b1), .Q(PC), .clk(CLK), .clr(RESET));
  Adder adder_1 (.a(PC), .b(8'h1), .out(adder_1_out));  // open: cin, cout
  Instruction_separator instruction_separator_1 (
    .Imm_Addr(out_12), .SHIFT_AMNT(out_11), .DST_REG(out_10), .SRC_REG2(out_9), .SRC_REG1(out_8),
    .OP_CODE(out_7), .Instruction(in_6));
  Adder adder_2 (.a(adder_1_out), .b(Shift_Amt), .out(adder_2_out));  // open: cin, cout
  Multiplexer #(.width(8)) multiplexer_1 (
    .in0(adder_1_out), .in1(adder_2_out), .out(multiplexer_1_out), .sel(in_2));  // open: en
  Multiplexer #(.width(8)) multiplexer_2 (
    .in0(multiplexer_1_out), .in1({out_8, out_9}), .out(multiplexer_2_out), .sel(in_3));  // open: en
endmodule

module Shifter (
  input  [7:0] Value,
  input  [3:0] SHAMT,
  input  in_3,
  output [7:0] Output
);

  wire [7:0] shifter_1_out, shifter_2_out;

  Shifter_part #(.shift("lr")) shifter_1 (.in(Value), .\dist (SHAMT[2:0]), .out(shifter_1_out));
  Shifter_part shifter_2 (.in(Value), .\dist (SHAMT[2:0]), .out(shifter_2_out));
  Multiplexer #(.width(8)) multiplexer_1 (
    .in0(shifter_1_out), .in1(shifter_2_out), .out(Output), .sel(in_3));  // open: en
endmodule
