// Logisim project 8bit ALU.circ as structural Verilog: 4 circuits, main circuit 1bit ALU
module _1bit_ALU (
  input  S0_prime,
  input  S1_prime,
  input  S2_prime,
  input  Cin,
  input  S2,
  input  S1,
  input  S0,
  input  A,
  input  B,
  output Sum,
  output Cout
);

  wire and_1_out, and_2_out, and_3_out, and_4_out, and_5_out, not_1_out, or_1_out, or_2_out;

  not not_1 (not_1_out, B);
  and and_1 (and_1_out, S2, S1_prime, S0_prime, B);
  and and_2 (and_2_out, S2, S1, S0_prime, not_1_out);
  and and_3 (and_3_out, S0, B);
  and and_4 (and_4_out, S1, not_1_out);
  or or_1 (or_1_out, and_1_out, and_2_out, A);
  or or_2 (or_2_out, and_3_out, and_4_out);
  and and_5 (and_5_out, Cin, S2_prime);
  Adder #(.width(1)) adder_1 (.a(or_1_out), .b(or_2_out), .out(Sum), .cin(and_5_out), .cout(Cout));
endmodule

module _4bit_ALU (
  input  [2:0] S2_S1_S0,
  input  Cin,
  input  [3:0] A,
  input  [3:0] B,
  output [3:0] Result,
  output Cout
);

  wire n1bit_alu_1_cout, n1bit_alu_2_cout, n1bit_alu_3_cout, not_1_out, not_2_out, not_3_out;

  not not_1 (not_1_out, S2_S1_S0[0]);
  not not_2 (not_2_out, S2_S1_S0[1]);
  not not_3 (not_3_out, S2_S1_S0[2]);
  _1bit_ALU u_1bit_alu_1 (
    .Cin(Cin), .S2(S2_S1_S0[2]), .S1(S2_S1_S0[1]), .S0(S2_S1_S0[0]), .A(A[0]), .B(B[0]), .Sum(Result[0]),
    .Cout(n1bit_alu_1_cout), .S0_prime(not_1_out), .S1_prime(not_2_out), .S2_prime(not_3_out));
  _1bit_ALU u_1bit_alu_2 (
    .Cin(n1bit_alu_1_cout), .S2(S2_S1_S0[2]), .S1(S2_S1_S0[1]), .S0(S2_S1_S0[0]), .A(A[1]), .B(B[1]),
    .Sum(Result[1]), .Cout(n1bit_alu_2_cout), .S0_prime(not_1_out), .S1_prime(not_2_out), .S2_prime(not_3_out));
  _1bit_ALU u_1bit_alu_3 (
    .Cin(n1bit_alu_2_cout), .S2(S2_S1_S0[2]), .S1(S2_S1_S0[1]), .S0(S2_S1_S0[0]), .A(A[2]), .B(B[2]),
    .Sum(Result[2]), .Cout(n1bit_alu_3_cout), .S0_prime(not_1_out), .S1_prime(not_2_out), .S2_prime(not_3_out));
  _1bit_ALU u_1bit_alu_4 (
    .Cin(n1bit_alu_3_cout), .S2(S2_S1_S0[2]), .S1(S2_S1_S0[1]), .S0(S2_S1_S0[0]), .A(A[3]), .B(B[3]),
    .Sum(Result[3]), .Cout(Cout), .S0_prime(not_1_out), .S1_prime(not_2_out), .S2_prime(not_3_out));
endmodule

module _8bit_ALU (
  input  [3:0] in_1,
  input  [7:0] A_8bit,
  input  [7:0] B_8bit,
  input  EN,
  input  CLK,
  input  CLR,
  output [7:0] Result,
  output out_8,
  output Cout
);

  wire n4bit_alu_1_cout, nor_1_out;

  _4bit_ALU u_4bit_alu_1 (
    .S2_S1_S0(in_1[3:1]), .Cin(in_1[0]), .A(A_8bit[3:0]), .B(B_8bit[3:0]), .Cout(n4bit_alu_1_cout),
    .Result(Result[3:0]));
  _4bit_ALU u_4bit_alu_2 (
    .S2_S1_S0(in_1[3:1]), .Cin(n4bit_alu_1_cout), .A(A_8bit[7:4]), .B(B_8bit[7:4]), .Cout(Cout),
    .Result(Result[7:4]));
  nor nor_1 (nor_1_out, Result[0], Result[1], Result[2], Result[3], Result[4], Result[5], Result[6], Result[7]);
  Register #(.width(1)) ZF (.D(nor_1_out), .en(EN), .Q(out_8), .clk(CLK), .clr(CLR));
endmodule

module _8bit_ALU_simulator (
  input  [3:0] Selection_bit,
  input  [7:0] Read_1,
  input  [7:0] Read_2__1,
  input  CLK,
  input  EN,
  input  CLR,
  output out_7,
  output [7:0] out_8,
  output ZF
);

  _8bit_ALU u_8bit_alu_1 (
    .A_8bit(Read_1), .B_8bit(Read_2__1), .Cout(out_7), .Result(out_8), .CLR(CLR), .EN(EN), .out_8(ZF),
    .CLK(CLK), .in_1(Selection_bit));
endmodule
