// Logisim project Processor.circ as structural Verilog: 11 circuits, main circuit main
module main (
  input  in_1,
  input  [3:0] in_2,
  input  [7:0] Load_Registers,
  output [7:0] Register_Values,
  output [7:0] out_5,
  output [7:0] out_6,
  output [7:0] out_7,
  output [7:0] out_8,
  output [7:0] out_9,
  output [7:0] out_10
);

  wire alu_src, alu_src_out, beq, bneq, Clock, EX_MEM_EN, jump, L_R_prime, m_read, m_write, mem_read,
       mem_to_reg, mem_wb_1_mem2reg, MEM_WB_EN, mem_write, \nor , or_1_out, or_2_out, reg_dst, reg_dst_out,
       reg_write, Reg_writeOut, reset, shift, TestCLK, zero_t;
  wire [1:0] RS_SELECT, RT_SELECT, WB;
  wire [3:0] alu_op, AluOp_OUT, EX_MEM_RD, M_WB, MEM_WB_RD, opcode, RD, RD_OUT, RS, RS_OUT, RT, RT_OUT,
       SHAMT, Write_Destination;
  wire [7:0] adder_1_out, alu_out, EX_MEM_OUT, FinalOutput, id_ex_1_out_19, id_ex_1_out_20,
       mem_wb_1_datamemout_2, MEM_WB_OUT, multiplexer_3_out, multiplexer_4_out, PC_q, R1, R2, ram_1_data,
       Write_Data;
  wire [19:0] rom_1_data;

  Button CLK (.out(Clock));
  Button u_Reset (.out(reset));
  Adder adder_1 (.a(8'h1), .b(PC_q), .out(adder_1_out));  // open: cin, cout
  Register #(.trigger("falling")) PC (.D(adder_1_out), .en(1'b1), .Q(PC_q), .clk(Clock), .clr(reset));
  ROM #(.dataWidth(20)) rom_1 (.addr(PC_q), .data(rom_1_data));  // open: sel
  IF_ID if_id_1 (
    .Instruction(rom_1_data), .CLK(Clock), .RESET(reset), .out_4(opcode), .out_5(RS), .out_6(RT), .out_7(RD),
    .out_8(SHAMT));
  Button button_1 (.out(TestCLK));
  or or_1 (or_1_out, Reg_writeOut, in_1);
  or or_2 (or_2_out, TestCLK, Clock);
  Registers registers_1 (
    .in_1(RS), .in_2(or_2_out), .in_3(or_1_out), .in_4(RT), .in_6(Write_Destination), .out_10(R1),
    .out_12(R2), .in_7(Write_Data), .in_5(reset), .out_8(Register_Values), .out_9(out_5), .out_11(out_6),
    .out_13(out_7), .out_14(out_8), .out_15(out_9), .out_16(out_10));
  Multiplexer #(.width(4)) multiplexer_1 (
    .in0(MEM_WB_RD), .in1(in_2), .out(Write_Destination), .sel(in_1));  // open: en
  Multiplexer #(.width(8)) multiplexer_2 (
    .in0(FinalOutput), .in1(Load_Registers), .out(Write_Data), .sel(in_1));  // open: en
  ID_EX id_ex_1 (
    .in_1(reg_dst), .AluSrc(alu_src), .ALUOp(alu_op), .Mem_Read(mem_read), .Mem_Write(mem_write),
    .Reg_Write(reg_write), .Mem2Reg(mem_to_reg), .CLK(Clock), .RESET(reset), .out_18(M_WB), .RS(RS), .RT(RT),
    .RD(RD), .out_21(RS_OUT), .out_22(RT_OUT), .out_23(RD_OUT), .Read_Data1(R1), .Read_Data2(R2),
    .out_19(id_ex_1_out_19), .out_20(id_ex_1_out_20), .ALU_OP(AluOp_OUT), .out_15(reg_dst_out),
    .AluSrc_2(alu_src_out));
  CONTROL control_1 (
    .OpCode(opcode), .Shift(shift), .JUMP(jump), .Left_Right_prime(L_R_prime), .BNEQ(bneq), .NOR(\nor ),
    .RegWrite(reg_write), .ALUSrc(alu_src), .MemWrite(mem_write), .ALUOp(alu_op), .MemtoReg(mem_to_reg),
    .MemRead(mem_read), .BEQ(beq), .RegDest(reg_dst));
  Multiplexer #(.select(2), .width(8)) multiplexer_3 (
    .in0(id_ex_1_out_20), .in2(MEM_WB_OUT), .in3(EX_MEM_OUT), .out(multiplexer_3_out), .sel(RT_SELECT));  // open: in1, en
  Multiplexer #(.select(2), .width(8)) multiplexer_4 (
    .in0(id_ex_1_out_19), .in2(MEM_WB_OUT), .in3(EX_MEM_OUT), .out(multiplexer_4_out), .sel(RS_SELECT));  // open: in1, en
  Forward_Unit forward_unit_1 (
    .RS(RS_OUT), .EX_MEM_RD(EX_MEM_RD), .MEM_WB_RD_(MEM_WB_RD), .RT(RT_OUT), .RS_select_bit(RS_SELECT),
    .RT_select_bit(RT_SELECT), .EX_MEM_EN(EX_MEM_EN), .MEM_WB_EN(MEM_WB_EN));
  _8bit_ALU u_8bit_alu_1 (
    .A_8bit(multiplexer_4_out), .B_8bit(multiplexer_3_out), .Result(alu_out), .CLR(reset), .EN(1'b1),
    .out_8(zero_t), .CLK(Clock), .in_1(AluOp_OUT));  // open: Cout
  EX_MEM ex_mem_1 (
    .in_1(M_WB), .ALU_Output(alu_out), .RD(RD_OUT), .CLK(Clock), .RESET(reset), .WB(WB), .mem_write(m_write),
    .mem_read(m_read), .out_9(EX_MEM_OUT), .out_10(EX_MEM_RD), .EX_MEM_EN(EX_MEM_EN));
  RAM #(.bus("separate")) ram_1 (
    .addr(EX_MEM_OUT), .din(R2), .data(ram_1_data), .str(m_write), .sel(1'b1), .clk(Clock), .ld(m_read));  // open: clr
  MEM_WB mem_wb_1 (
    .WB(WB), .ALUOut(EX_MEM_OUT), .EX_MEM_RegRD(EX_MEM_RD), .DataMemOut_2(mem_wb_1_datamemout_2),
    .ALUOut_2(MEM_WB_OUT), .EX_MEM_RegRD_2(MEM_WB_RD), .CLK(Clock), .Reset(reset),
    .Mem2Reg(mem_wb_1_mem2reg), .Reg_Write(Reg_writeOut), .MEM_WB_EN(MEM_WB_EN), .DataMemOut(ram_1_data));
  Multiplexer #(.width(8)) multiplexer_5 (
    .in0(MEM_WB_OUT), .in1(mem_wb_1_datamemout_2), .out(FinalOutput), .sel(mem_wb_1_mem2reg));  // open: en

  // Other names for the same wires on the sheet: LoadRegData[7:0] = Load_Registers; LoadRegEN = in_1;
  //   sp[7:0] = out_10; t0[7:0] = Register_Values; t1[7:0] = out_5; t2[7:0] = out_6; t3[7:0] = out_7; t4[7:0] = out_8;
  //   TestDest[3:0] = in_2; zero[7:0] = out_9

  // Notes on the sheet:
  //   contents of rom_1 (hex, n*v repeats v):
  //   22310 d1240 f1340 24330 24300 d0310 c1340 21400 c0120 d2030
  //   2
  //   0
  //   5
  //   DATA-Memory
endmodule

module Registers (
  input  [3:0] in_1,
  input  in_2,
  input  in_3,
  input  [3:0] in_4,
  input  in_5,
  input  [3:0] in_6,
  input  [7:0] in_7,
  output [7:0] out_8,
  output [7:0] out_9,
  output [7:0] out_10,
  output [7:0] out_11,
  output [7:0] out_12,
  output [7:0] out_13,
  output [7:0] out_14,
  output [7:0] out_15,
  output [7:0] out_16
);

  wire demultiplexer_1_out0, demultiplexer_1_out1, demultiplexer_1_out2, demultiplexer_1_out3,
       demultiplexer_1_out4, demultiplexer_1_out5, demultiplexer_1_out6, or_1_out, stack_en, stack_selector;
  wire [7:0] register_8_q, stack_d;

  Multiplexer multiplexer_1 (.in0(stack_selector), .in1(1'b1), .out(stack_en), .sel(in_5));  // open: en
  Multiplexer #(.width(8)) multiplexer_2 (.in0(in_7), .in1({8{1'b1}}), .out(stack_d), .sel(in_5));  // open: en
  Demultiplexer #(.select(4)) demultiplexer_1 (
    .out0(demultiplexer_1_out0), .out1(demultiplexer_1_out1), .out2(demultiplexer_1_out2),
    .out3(demultiplexer_1_out3), .out4(demultiplexer_1_out4), .out5(demultiplexer_1_out5),
    .out6(demultiplexer_1_out6), .out7(stack_selector), .in(in_3), .sel(in_6), .en(1'b1));  // open: out8, out9, out10, out11, out12, out13, out14, out15
  Register register_1 (.D(in_7), .en(demultiplexer_1_out0), .Q(out_8), .clk(in_2), .clr(in_5));
  Register register_2 (.D(in_7), .en(demultiplexer_1_out3), .Q(out_13), .clk(in_2), .clr(in_5));
  Register register_3 (.D(in_7), .en(demultiplexer_1_out1), .Q(out_9), .clk(in_2), .clr(in_5));
  Register register_4 (.D(in_7), .en(demultiplexer_1_out4), .Q(out_14), .clk(in_2), .clr(in_5));
  Register register_5 (.D(in_7), .en(demultiplexer_1_out2), .Q(out_11), .clk(in_2), .clr(in_5));
  Register register_6 (.D({8{1'b0}}), .en(demultiplexer_1_out5), .Q(out_15), .clk(in_2), .clr(in_5));
  or or_1 (or_1_out, in_5, in_2);
  Register #(.trigger("falling")) register_7 (.D(stack_d), .en(stack_en), .Q(out_16), .clk(or_1_out));  // open: clr
  Register #(.trigger("falling")) register_8 (
    .D(in_7), .en(demultiplexer_1_out6), .Q(register_8_q), .clk(in_2), .clr(in_5));
  Multiplexer #(.select(4), .width(8)) multiplexer_3 (
    .in0(out_8), .in1(out_9), .in2(out_11), .in3(out_13), .in4(out_14), .in5(out_15), .in6(register_8_q),
    .in7(out_16), .out(out_10), .sel(in_1));  // open: in8, in9, in10, in11, in12, in13, in14, in15, en
  Multiplexer #(.select(4), .width(8)) multiplexer_4 (
    .in0(out_8), .in1(out_9), .in2(out_11), .in3(out_13), .in4(out_14), .in5(out_15), .in6(register_8_q),
    .in7(out_16), .out(out_12), .sel(in_4));  // open: in8, in9, in10, in11, in12, in13, in14, in15, en

  // Other names for the same wires on the sheet: clk = in_2; reg1_i[3:0] = in_1; reg1_o[7:0] = out_10;
  //   reg2_i[3:0] = in_4; reg2_o[7:0] = out_12; Reset = in_5; sp[7:0] = out_16; t0[7:0] = out_8; t1[7:0] = out_9;
  //   t2[7:0] = out_11; t3[7:0] = out_13; t4[7:0] = out_14; WE = in_3; write_data[7:0] = in_7; write_reg[3:0] = in_6;
  //   zero[7:0] = out_15
endmodule

module CONTROL (
  input  [3:0] OpCode,
  output Shift,
  output JUMP,
  output Left_Right_prime,
  output BNEQ,
  output NOR,
  output RegWrite,
  output ALUSrc,
  output MemWrite,
  output [3:0] ALUOp,
  output MemtoReg,
  output MemRead,
  output BEQ,
  output RegDest
);

  ROM #(.addrWidth(4), .dataWidth(16)) rom_1 (
    .addr(OpCode),
    .data({RegDest, BEQ, MemRead, MemtoReg, ALUOp, MemWrite, ALUSrc, RegWrite, NOR, BNEQ, Left_Right_prime, JUMP, Shift}));  // open: sel

  // Notes on the sheet:
  //   contents of rom_1 (hex, n*v repeats v):
  //   0 c60 8220 260 560 4500 8830 3260 2 508 12e0 8025 8c20 8520 8021 8820
endmodule

module Instruction_separator (
  input  [19:0] Instruction,
  output [7:0] Instr_Addr,
  output [3:0] SHIFT_AMNT,
  output [3:0] DST_REG,
  output [3:0] SRC_REG2,
  output [3:0] SRC_REG1,
  output [3:0] OP_CODE
);


  assign DST_REG = Instruction[7:4];
  assign Instr_Addr = Instruction[7:0];
  assign OP_CODE = Instruction[19:16];
  assign SHIFT_AMNT = Instruction[3:0];
  assign SRC_REG1 = Instruction[15:12];
  assign SRC_REG2 = Instruction[11:8];
endmodule

module Instruction_Counter (
  input  RESET,
  input  CLK,
  output [7:0] PC
);

  wire [7:0] adder_1_out;

  Register #(.trigger("falling")) u_PC (.D(adder_1_out), .en(1'b1), .Q(PC), .clk(CLK), .clr(RESET));
  Adder adder_1 (.a(PC), .b(8'h1), .out(adder_1_out));  // open: cin, cout
endmodule

module Shifter (
  input  [7:0] Value,
  input  [3:0] SHAMT,
  input  in_3,
  output [7:0] Output
);

  wire [7:0] shifter_1_out, shifter_2_out;

  Shifter_part #(.shift("lr")) shifter_1 (.in(Value), .\dist (SHAMT[2:0]), .out(shifter_1_out));
  Shifter_part shifter_2 (.in(Value), .\dist (SHAMT[2:0]), .out(shifter_2_out));
  Multiplexer #(.width(8)) multiplexer_1 (
    .in0(shifter_1_out), .in1(shifter_2_out), .out(Output), .sel(in_3));  // open: en
endmodule

module IF_ID (
  input  [19:0] Instruction,
  input  CLK,
  input  RESET,
  output [3:0] out_4,
  output [3:0] out_5,
  output [3:0] out_6,
  output [3:0] out_7,
  output [3:0] out_8
);

  wire [19:0] register_1_q;

  Register #(.width(20), .trigger("falling")) register_1 (
    .D(Instruction), .en(1'b1), .Q(register_1_q), .clk(CLK), .clr(RESET));
  Instruction_separator instruction_separator_1 (
    .SHIFT_AMNT(out_8), .DST_REG(out_7), .SRC_REG2(out_6), .SRC_REG1(out_5), .OP_CODE(out_4),
    .Instruction(register_1_q));  // open: Instr_Addr
endmodule

// Reg_Dest
module ID_EX (
  input  in_1,
  input  AluSrc,
  input  [3:0] ALUOp,
  input  Mem_Read,
  input  Mem_Write,
  input  Reg_Write,
  input  Mem2Reg,
  input  [7:0] Read_Data1,
  input  [7:0] Read_Data2,
  input  [3:0] RS,
  input  [3:0] RT,
  input  [3:0] RD,
  input  CLK,
  input  RESET,
  output out_15,
  output AluSrc_2,
  output [3:0] ALU_OP,
  output [3:0] out_18,
  output [7:0] out_19,
  output [7:0] out_20,
  output [3:0] out_21,
  output [3:0] out_22,
  output [3:0] out_23
);

  Register #(.width(6), .trigger("falling")) register_1 (
    .D({ALUOp, AluSrc, in_1}), .en(1'b1), .Q({ALU_OP, AluSrc_2, out_15}), .clk(CLK), .clr(RESET));
  Register #(.width(4), .trigger("falling")) register_2 (
    .D({Mem_Read, Mem_Write, Reg_Write, Mem2Reg}), .en(1'b1), .Q(out_18), .clk(CLK), .clr(RESET));
  Register #(.trigger("falling")) register_3 (.D(Read_Data1), .en(1'b1), .Q(out_19), .clk(CLK), .clr(RESET));
  Register #(.trigger("falling")) register_4 (.D(Read_Data2), .en(1'b1), .Q(out_20), .clk(CLK), .clr(RESET));
  Register #(.width(4), .trigger("falling")) register_5 (.D(RS), .en(1'b1), .Q(out_21), .clk(CLK), .clr(RESET));
  Register #(.width(4), .trigger("falling")) register_6 (.D(RT), .en(1'b1), .Q(out_22), .clk(CLK), .clr(RESET));
  Register #(.width(4), .trigger("falling")) register_7 (.D(RD), .en(1'b1), .Q(out_23), .clk(CLK), .clr(RESET));
endmodule

module EX_MEM (
  input  [3:0] in_1,
  input  [7:0] ALU_Output,
  input  [3:0] RD,
  input  CLK,
  input  RESET,
  output [1:0] WB,
  output mem_write,
  output mem_read,
  output [7:0] out_9,
  output [3:0] out_10,
  output EX_MEM_EN
);

  wire [7:0] counter_1_q;

  Register #(.width(4), .trigger("falling")) register_1 (
    .D(in_1), .en(1'b1), .Q({mem_read, mem_write, WB}), .clk(CLK), .clr(RESET));
  Register #(.trigger("falling")) register_2 (.D(ALU_Output), .en(1'b1), .Q(out_9), .clk(CLK), .clr(RESET));
  Register #(.width(4), .trigger("falling")) register_3 (.D(RD), .en(1'b1), .Q(out_10), .clk(CLK), .clr(RESET));
  Counter #(.trigger("falling")) counter_1 (
    .D({8{1'b0}}), .count(1'b1), .Q(counter_1_q), .clk(CLK), .clr(RESET));  // open: load, carry
  Comparator comparator_1 (.a(counter_1_q), .b(8'h2), .gt(EX_MEM_EN));  // open: eq, lt
endmodule

module MEM_WB (
  input  CLK,
  input  Reset,
  input  [1:0] WB,
  input  [7:0] DataMemOut,
  input  [7:0] ALUOut,
  input  [3:0] EX_MEM_RegRD,
  output Mem2Reg,
  output Reg_Write,
  output [7:0] DataMemOut_2,
  output [7:0] ALUOut_2,
  output [3:0] EX_MEM_RegRD_2,
  output MEM_WB_EN
);

  wire [7:0] counter_1_q;

  Register #(.width(2), .trigger("falling")) register_1 (
    .D(WB), .en(1'b1), .Q({Reg_Write, Mem2Reg}), .clk(CLK), .clr(Reset));
  Register #(.trigger("falling")) register_2 (.D(DataMemOut), .en(1'b1), .Q(DataMemOut_2), .clk(CLK), .clr(Reset));
  Register #(.trigger("falling")) register_3 (.D(ALUOut), .en(1'b1), .Q(ALUOut_2), .clk(CLK), .clr(Reset));
  Register #(.width(4), .trigger("falling")) register_4 (
    .D(EX_MEM_RegRD), .en(1'b1), .Q(EX_MEM_RegRD_2), .clk(CLK), .clr(Reset));
  Counter #(.trigger("falling")) counter_1 (
    .D({8{1'b0}}), .count(1'b1), .Q(counter_1_q), .clk(CLK), .clr(Reset));  // open: load, carry
  Comparator comparator_1 (.a(counter_1_q), .b(8'h3), .gt(MEM_WB_EN));  // open: eq, lt
endmodule

module Forward_Unit (
  input  [3:0] RS,
  input  [3:0] EX_MEM_RD,
  input  [3:0] MEM_WB_RD_,
  input  [3:0] RT,
  input  EX_MEM_EN,
  input  MEM_WB_EN,
  output [1:0] RS_select_bit,
  output [1:0] RT_select_bit
);

  wire comparator_1_eq, comparator_2_eq, comparator_3_eq, comparator_4_eq, multiplexer_2_out,
       multiplexer_4_out;

  Comparator #(.width(4)) comparator_1 (.a(RS), .b(EX_MEM_RD), .eq(comparator_1_eq));  // open: gt, lt
  Comparator #(.width(4)) comparator_2 (.a(RS), .b(MEM_WB_RD_), .eq(comparator_2_eq));  // open: gt, lt
  Comparator #(.width(4)) comparator_3 (.a(RT), .b(EX_MEM_RD), .eq(comparator_3_eq));  // open: gt, lt
  Comparator #(.width(4)) comparator_4 (.a(RT), .b(MEM_WB_RD_), .eq(comparator_4_eq));  // open: gt, lt
  Multiplexer multiplexer_1 (.in0(1'b0), .in1(comparator_1_eq), .out(RS_select_bit[0]), .sel(EX_MEM_EN));  // open: en
  Multiplexer multiplexer_2 (.in0(1'b0), .in1(comparator_2_eq), .out(multiplexer_2_out), .sel(MEM_WB_EN));  // open: en
  Multiplexer multiplexer_3 (.in0(1'b0), .in1(comparator_3_eq), .out(RT_select_bit[0]), .sel(EX_MEM_EN));  // open: en
  Multiplexer multiplexer_4 (.in0(1'b0), .in1(comparator_4_eq), .out(multiplexer_4_out), .sel(MEM_WB_EN));  // open: en
  or or_1 (RS_select_bit[1], RS_select_bit[0], multiplexer_2_out);
  or or_2 (RT_select_bit[1], RT_select_bit[0], multiplexer_4_out);
endmodule
