// Logisim project off 1.circ as structural Verilog
module ALU_1 (
  input  Ci,
  input  CS1,
  input  Ai,
  input  Bi,
  input  CS0,
  output out_6,
  output out_7
);

  wire and_1_out, not_1_out, not_2_out, or_1_out;

  not not_1 (not_1_out, CS1);
  not not_2 (not_2_out, CS0);
  or or_1 (or_1_out, Bi, not_2_out);
  and and_1 (and_1_out, not_1_out, Ci);
  Adder #(.width(1)) adder_1 (.a(Ai), .b(or_1_out), .out(out_6), .cin(and_1_out), .cout(out_7));
endmodule

module _4_bit_ALU (
  input  [3:0] A,
  input  [3:0] B,
  input  [2:0] CS2_CS1_CS0,
  output [3:0] out_4,
  output out_5
);

  wire alu_1_1_out_7, alu_1_2_out_7, alu_1_3_out_7;

  ALU_1 alu_1_1 (
    .Ci(CS2_CS1_CS0[2]), .CS1(CS2_CS1_CS0[1]), .Ai(A[0]), .Bi(B[0]), .CS0(CS2_CS1_CS0[0]), .out_6(out_4[0]),
    .out_7(alu_1_1_out_7));
  ALU_1 alu_1_2 (
    .Ci(alu_1_1_out_7), .CS1(CS2_CS1_CS0[1]), .Ai(A[1]), .Bi(B[1]), .CS0(CS2_CS1_CS0[0]), .out_6(out_4[1]),
    .out_7(alu_1_2_out_7));
  ALU_1 alu_1_3 (
    .Ci(alu_1_2_out_7), .CS1(CS2_CS1_CS0[1]), .Ai(A[2]), .Bi(B[2]), .CS0(CS2_CS1_CS0[0]), .out_6(out_4[2]),
    .out_7(alu_1_3_out_7));
  ALU_1 alu_1_4 (
    .Ci(alu_1_3_out_7), .CS1(CS2_CS1_CS0[1]), .Ai(A[3]), .Bi(B[3]), .CS0(CS2_CS1_CS0[0]), .out_6(out_4[3]),
    .out_7(out_5));
endmodule
