// Logisim project prac1.circ as structural Verilog: 2 circuits, main circuit ALU 1-bit
module ALU_1_bit (
  input  CS2,
  input  CS1,
  input  Ai,
  input  Bi,
  input  CS0,
  output out_6,
  output out_7
);

  wire and_1_out, not_1_out, not_2_out, or_1_out;

  not not_1 (not_1_out, CS0);
  not not_2 (not_2_out, CS1);
  and and_1 (and_1_out, CS2, not_2_out);
  or or_1 (or_1_out, Bi, not_1_out);
  Adder #(.width(1)) adder_1 (.a(Ai), .b(or_1_out), .out(out_6), .cin(and_1_out), .cout(out_7));
endmodule

module ALU_4_bit (
  input  [3:0] A,
  input  [3:0] B,
  input  [2:0] CS,
  output [3:0] out_4,
  output [3:0] out_5,
  output out_6
);

  wire alu_1_bit_1_out_7, alu_1_bit_2_out_7, alu_1_bit_3_p6, alu_1_bit_4_out_7, clock_1_out, not_1_out,
       undriven, xor_1_out;

  not not_1 (not_1_out, CS[1]);
  ALU_1_bit alu_1_bit_1 (
    .CS2(CS[2]), .CS1(CS[1]), .Ai(A[0]), .Bi(B[0]), .CS0(CS[0]), .out_6(out_4[0]), .out_7(alu_1_bit_1_out_7));
  ALU_1_bit alu_1_bit_2 (
    .CS2(alu_1_bit_1_out_7), .CS1(CS[1]), .Ai(A[1]), .Bi(B[1]), .CS0(CS[0]), .out_6(out_4[1]),
    .out_7(alu_1_bit_2_out_7));
  // ALU_1_bit alu_1_bit_3: pin names not known; wires that end beside it: CS[0], CS[1], alu_1_bit_2_out_7, A[2], B[2], alu_1_bit_3_p6, out_4[2]
  ALU_1_bit alu_1_bit_4 (
    .CS2(alu_1_bit_3_p6), .CS1(CS[1]), .Ai(A[3]), .Bi(B[3]), .CS0(CS[0]), .out_6(out_4[3]),
    .out_7(alu_1_bit_4_out_7));
  xor xor_1 (xor_1_out, alu_1_bit_3_p6, alu_1_bit_4_out_7);
  D_Flip_Flop d_ff_1 (.clk(clock_1_out), .D(xor_1_out), .Q(out_6), .en(not_1_out));  // open: Qn, preset, reset
  D_Flip_Flop d_ff_2 ();  // open: clk, D, Q, Qn, preset, en, reset
  D_Flip_Flop d_ff_3 ();  // open: clk, D, Q, Qn, preset, en, reset
  D_Flip_Flop d_ff_4 (.clk(undriven));  // open: D, Q, Qn, preset, en, reset
  Clock clock_1 (.out(clock_1_out));
endmodule
